# Fritzing sketch Esquematico (saved by Fritzing 0.9.3b)
breadboards: 2

parts:
  Part1 = Arduino Uno (Rev3) - ICSP
  Part2 = Soil Moisture Sensor
  U1 = G3VM-61E1 [package=g3vm-61e1]
  RHT1 = Humidity and Temperature Sensor RHT03
  M1 = DC Motor  # not connected
  Part3 = Bluetooth HC-05 Macho
  R1 = Resistor [tolerance=±5% resistance=220 package=THT]
  LED2 = smd LED [color="Red (633nm)" package="1206 [SMD]"]
  R2 = Resistor [tolerance=±5% resistance=220 package="2512 [SMD]"]
  S1 = Round Pushbutton

nets:
  N1: Part1.A0, Part2.SIG
  N2: Part1.ICSP_MISO, Part1.D12/MISO, Part3.VCC
  N3: Part1.D8, U1.P$4
  N4: Part1.D9_PWM, RHT1.GND_1, R2.Pin_0
  N5: Part1.D0/RX, Part3.TXD
  N6: Part1.D1/TX, Part3.RXD
  N7: Part1.D3_PWM, S1.leg1
  N8: Part1.D4, LED2.anode
  N9: Part1.3V3, U1.P$1, U1.P$5
  5V: Part1.5V, Part2.VCC, RHT1.GND_2
  GND: Part1.GND, Part2.GND, U1.P$6, RHT1.Data-signal, Part3.GND, R1.Pin_0, R2.Pin_1, S1.leg0
  N10: R1.Pin_1, LED2.cathode

notes:
  Este es el HC-05, pero se uso el HC-06 que no cuenta con Key ni State
  +5V
  GND
  +3.3V
  Este es el RHT1 pero se uso el DHT11 que solo tiene 3 patillas: VCC, DATA y GND
  s
  +
  -
  NC
  COMMON
  NA
  +
  -
  Este simula el sensor de nivel
