# Fritzing sketch Prototipo_Jardin (saved by Fritzing 0.9.3b)
breadboards: 1

parts:
  Part1 = Arduino Uno (Rev3)
  RELAY1 = CAR RELAY [part_number=NVF4-2 package=THT]  # not connected
  BAT1 = Battery Holders [package=battery-aa]
  M1 = DC Motor
  Part2 = Soil Moisture Sensor

nets:
  N1: Part1.A0, Part2.SIG
  5V: Part1.5V, Part2.VCC
  GND: Part1.GND, Part2.GND
  N2: BAT1.-, M1.pin_1

notes:
  NC
  COMUN
  NA
  S
  +
  -
